// Logisim project Atv_1.circ as structural Verilog: 1 circuit, main circuit main
module main (
  input  A,
  input  C,
  input  E,
  input  A_2,
  input  B,
  input  C_2,
  input  G
);

  wire and_1_out, and_2_out, and_3_out, and_4_out, and_5_out, clock_1_out, clock_2_out, clock_3_out,
       clock_4_out, clock_5_out, or_1_out, or_2_out, or_3_out;

  Clock #(.highDuration(3)) clock_1 (.out(clock_1_out));
  Clock #(.highDuration(3)) clock_2 (.out(clock_2_out));
  Clock #(.highDuration(3)) clock_3 (.out(clock_3_out));
  Clock clock_4 (.out(clock_4_out));
  Clock #(.highDuration(2), .lowDuration(2)) clock_5 (.out(clock_5_out));
  or or_1 (or_1_out, A, clock_1_out);
  or or_2 (or_2_out, C, clock_2_out);
  and and_1 (and_1_out, E, clock_3_out);
  and and_2 (and_2_out, A_2, B, C_2);
  or or_3 (or_3_out, clock_4_out, clock_5_out);
  and and_3 (and_3_out, or_1_out, or_2_out);
  and and_4 (and_4_out, and_2_out, or_3_out, G);
  and and_5 (and_5_out, and_3_out, and_1_out);
  LED led_1 (.in(and_4_out));
  LED led_2 (.in(and_5_out));

  // Notes on the sheet:
  //   B
  //   D
  //   F
  //   D
  //   E
  //   S1
  //   S2
  //   S3
  //   S4
  //   S
  //   LED
endmodule
